# Fritzing sketch FirstSetUp (saved by Fritzing 0.9.3b)
circuit board: 8.46667cm x 5.64444cm
breadboards: 2

parts:
  Part9 = EasyDriver_v44
  Part10 = EasyDriver_v44
  M8 = Stepper Motor - Bipolar
  M12 = Stepper Motor - Bipolar
  Part13 = Arduino Nano (Rev3.0)
  Part14 = EasyDriver_v44
  M13 = Stepper Motor - Bipolar
  M14 = Stepper Motor - Bipolar
  Part15 = EasyDriver_v44

nets:
  GND: Part9.GND, Part10.GND, Part14.GND, Part15.GND
  N1: Part9.V+, Part10.V+, Part14.V+, Part15.V+
  N2: Part9.STEP, Part13.D2
  N3: Part9.DIR, Part13.D3
  N4: Part9.OUT2A, M12.A
  N5: Part9.OUT2B, M12.C
  N6: Part9.OUT1A, M12.D
  N7: Part9.OUT1B, M12.B
  N8: Part10.STEP, Part13.D4
  N9: Part10.DIR, Part13.D5
  N10: Part10.OUT2A, M8.A
  N11: Part10.OUT2B, M8.C
  N12: Part10.OUT1A, M8.D
  N13: Part10.OUT1B, M8.B
  N14: Part13.D6, Part15.STEP
  N15: Part13.D7, Part15.DIR
  N16: Part13.D8, Part14.STEP
  N17: Part13.D9, Part14.DIR
  GND_2: Part13.GND
  5V: Part13.5V
  N18: Part14.OUT2A, M13.A
  N19: Part14.OUT2B, M13.C
  N20: Part14.OUT1A, M13.D
  N21: Part14.OUT1B, M13.B
  N22: M14.A, Part15.OUT2A
  N23: M14.C, Part15.OUT2B
  N24: M14.B, Part15.OUT1B
  N25: M14.D, Part15.OUT1A
