# Fritzing sketch newparts (saved by Fritzing 0.9.3b)
breadboards: 1

parts:
  X1 = X113647 Stepper Driver Board [package=board]
  Part1 = Arduino Nano (Rev3.0) (ICSP)
  KEYPAD1 = Membrane Matrix Keypad  # not connected
  X2 = X113647 Stepper Driver Board [package=board]
  X3 = X113647 Stepper Driver Board [package=board]
  X4 = X113647 Stepper Driver Board [package=board]
  MOTOR3 = 28BYJ-48 Stepper Motor
  MOTOR4 = 28BYJ-48 Stepper Motor
  MOTOR5 = 28BYJ-48 Stepper Motor
  MOTOR6 = 28BYJ-48 Stepper Motor
  Power_plug1 = Power plug

nets:
  N1: X1.BLUE, MOTOR3.BLUE
  N2: X1.PINK, MOTOR3.PINK
  N3: X1.YELLOW, MOTOR3.YELLOW
  N4: X1.ORANGE, MOTOR3.ORANGE
  N5: X1.RED, MOTOR3.RED
  N6: Part1.D2, X4.IN1
  N7: Part1.D3, X4.IN2
  N8: Part1.D4, X4.IN3
  N9: Part1.D5, X4.IN4
  N10: X2.BLUE, MOTOR6.BLUE
  N11: X2.PINK, MOTOR6.PINK
  N12: X2.YELLOW, MOTOR6.YELLOW
  N13: X2.ORANGE, MOTOR6.ORANGE
  N14: X2.RED, MOTOR6.RED
  N15: X3.BLUE, MOTOR5.BLUE
  N16: X3.PINK, MOTOR5.PINK
  N17: X3.YELLOW, MOTOR5.YELLOW
  N18: X3.ORANGE, MOTOR5.ORANGE
  N19: X3.RED, MOTOR5.RED
  N20: X4.+V, Power_plug1.VCC
  N21: X4.BLUE, MOTOR4.BLUE
  N22: X4.PINK, MOTOR4.PINK
  N23: X4.YELLOW, MOTOR4.YELLOW
  N24: X4.ORANGE, MOTOR4.ORANGE
  N25: X4.RED, MOTOR4.RED

custom parts:
  X113647 Stepper Driver Board: A common stepper motor driver board based on ULN2003APG darlington array
  Membrane Matrix Keypad: Membrane Matrix 3x4 Keypad
  28BYJ-48 Stepper Motor: 28BYJ-48 gear-reduction stepper motor (small)
